# Fritzing sketch lampomatic (saved by Fritzing 0.9.3b)
breadboards: 1

parts:
  WeMos_D1_Mini1 = WeMos D1 Mini
  Q1 = NPN-Transistor [part_number=BC337 package="TO92 [THT]"]
  Q2 = NPN-Transistor [part_number=BC337 package="TO92 [THT]"]
  R1 = Resistor [tolerance=±5% resistance=560 package=THT]
  R2 = Resistor [tolerance=±5% resistance=560 package=THT]
  LED1 = LED - 5mm [color="Red (633nm)" package="5 mm [THT]"]
  LED2 = LED - 5mm [color="Red (633nm)" package="5 mm [THT]"]
  LED3 = LED - 5mm [color="Red (633nm)" package="5 mm [THT]"]
  LED4 = LED - 5mm [color="Red (633nm)" package="5 mm [THT]"]
  LED5 = LED - 5mm [color="Red (633nm)" package="5 mm [THT]"]
  LED6 = LED - 5mm [color="Red (633nm)" package="5 mm [THT]"]
  LED7 = LED - 5mm [color="Red (633nm)" package="5 mm [THT]"]
  LED8 = LED - 5mm [color="Red (633nm)" package="5 mm [THT]"]
  R3 = Resistor [tolerance=±5% resistance=150 package=THT]
  R4 = Resistor [tolerance=±5% resistance=150 package=THT]
  R5 = Resistor [tolerance=±5% resistance=150 package=THT]
  R6 = Resistor [tolerance=±5% resistance=150 package=THT]
  LED9 = LED - 3mm [color="Blue (470nm)" package="3 mm [THT]"]
  LED10 = LED - 3mm [color="Blue (470nm)" package="3 mm [THT]"]
  LED11 = LED - 3mm [color="Blue (470nm)" package="3 mm [THT]"]
  LED12 = LED - 3mm [color="Blue (470nm)" package="3 mm [THT]"]
  R7 = Resistor [tolerance=±5% resistance=68 package=THT]
  R8 = Resistor [tolerance=±5% resistance=68 package=THT]
  R9 = Resistor [tolerance=±5% resistance=68 package=THT]
  R10 = Resistor [tolerance=±5% resistance=68 package=THT]
  R11 = Resistor [tolerance=±5% resistance=10k package=THT]
  R12 = Resistor [tolerance=±5% resistance=10k package=THT]

nets:
  N1: WeMos_D1_Mini1.5V, R3.Pin_1, R4.Pin_1, R5.Pin_1, R6.Pin_1, R7.Pin_1, R8.Pin_1, R9.Pin_1, R10.Pin_1
  N2: WeMos_D1_Mini1.D1, R1.Pin_0
  N3: WeMos_D1_Mini1.D2, R2.Pin_0
  N4: WeMos_D1_Mini1.G, Q1.E, Q2.E, R11.Pin_1, R12.Pin_1
  N5: Q1.B, R1.Pin_1, R11.Pin_0
  N6: Q1.C, LED2.cathode, LED4.cathode, LED6.cathode, LED8.cathode
  N7: Q2.B, R2.Pin_1, R12.Pin_0
  N8: Q2.C, LED9.cathode, LED10.cathode, LED11.cathode, LED12.cathode
  N9: LED1.cathode, LED2.anode
  N10: LED1.anode, R3.Pin_0
  N11: LED3.cathode, LED4.anode
  N12: LED3.anode, R4.Pin_0
  N13: LED5.cathode, LED6.anode
  N14: LED5.anode, R5.Pin_0
  N15: LED7.cathode, LED8.anode
  N16: LED7.anode, R6.Pin_0
  N17: LED9.anode, R7.Pin_0
  N18: LED10.anode, R8.Pin_0
  N19: LED11.anode, R9.Pin_0
  N20: LED12.anode, R10.Pin_0
